# Fritzing sketch CONDUITS_Fritzing (saved by Fritzing 0.9.9b)
circuit board: 3.89cm x 6.30913cm
breadboards: 1

parts:
  arduino = Arduino Pro Mini v13
  Rpu = Resistor [tolerance=±5% power=0.25 resistance=220 package=THT]
  Rw = Resistor [tolerance=±5% power=0.25 resistance=220 package=THT]
  Rg = Resistor [tolerance=±5% power=0.25 resistance=220 package=THT]
  Rr = Resistor [tolerance=±5% power=0.25 resistance=220 package=THT]
  LEDw = LED - 3mm [color="Infrared (850nm)" current=0.030 package="3 mm [THT]"]
  LEDg = LED - 3mm [color="Yellow (595nm)" current=0.030 package="3 mm [THT]"]
  LEDr = LED - 3mm [color="Red (633nm)" current=0.030 package="3 mm [THT]"]
  power = female pin header, 2 pins [form="♀ (female)"]
  mat = female pin header, 2 pins [form="♀ (female)"]
  remote = female pin header, 3 pins [form="♀ (female)"]
  battery = Battery Holders [package=battcom_20mm_pth]
  bluetooth = Bluetooth HC-06u [package=THT]
  D1 = Rectifier Diode [part_number=1N4001 package="300 mil [THT]"]

nets:
  N1: arduino.VCC, D1.cathode
  GND: arduino.GND, Rpu.Pin_0, Rw.Pin_0, Rg.Pin_0, Rr.Pin_0, power.pin1, remote.pin3, battery.-, bluetooth.GND
  N2: arduino.D12/MISO, remote.pin1
  N3: arduino.D11_PWM/MOSI, remote.pin2
  N4: arduino.D10_PWM/SS, arduino.D5_PWM, arduino.D4, bluetooth.VCC
  N5: arduino.D9_PWM, LEDr.anode
  N6: arduino.D8, bluetooth.TXD
  N7: arduino.D7, bluetooth.RXD
  N8: arduino.D6_PWM, LEDg.anode
  N9: arduino.D3_PWM, LEDw.anode
  N10: arduino.D2, Rpu.Pin_1, mat.pin1
  N11: Rw.Pin_1, LEDw.cathode
  N12: Rg.Pin_1, LEDg.cathode
  N13: Rr.Pin_1, LEDr.cathode
  N14: power.pin2, mat.pin2, battery.+, D1.anode

notes:
  + -
  G U L
  +
  -
  vcc
  rx
  tx
  gnd
  Jeanelle Dao  CONDUITS  Sept 2022

custom parts:
  Bluetooth HC-06u: Bluetooth HC-06 - face up, pins down 16.5mm x 37.5mm PCB
